# Fritzing sketch BUTTON (saved by Fritzing 0.8.7b)

parts:
  Parte1 = Arduino Mega 2560 (Rev3)
  S1 = Square Pushbutton
  R1 = Resistor [package="2010 [SMD]"]

nets:
  N1: Parte1.GND, R1.Pin_0
  N2: Parte1.D10_PWM, Parte1.5V, S1.leg0, S1.leg1, R1.Pin_1
