# Fritzing sketch DHT11 (saved by Fritzing 0.8.7b)
breadboards: 1

parts:
  Mod1 = KY-015 Temperature & Humidity Sensor Module [package="Breakout board"]
  Parte1 = Arduino Mega ADK (Rev3)

nets:
  N1: Mod1.S, Parte1.D6_PWM
  VIN: Mod1.Vin, Parte1.5V
  N2: Mod1.-, Parte1.GND

custom parts:
  KY-015 Temperature & Humidity Sensor Module: KY-015 temperature and humidity sensor module, provides a low-latency serial interface to measure humidity and temperature.
