# Fritzing sketch ESP32 (saved by Fritzing 0.8.7b)

parts:
  U1 = ESP32-38PinWide [part_number=ESP32-38PinWide]
  Parte1 = Arduino Mega ADK (Rev3)

nets:
  N1: U1.GPIO3, Parte1.D18/TX1
  N2: U1.GPIO1, Parte1.D19/RX1

custom parts:
  ESP32-38PinWide: Generic 38-Pin ESP32 with wide format (only access to one side of pins on a breadboard) based on Stephen Lilley's HiLetgo ESP-WROOM-32 ESP32 ESP-32S Development Board.
