# Fritzing sketch PIR (saved by Fritzing 0.8.7b)

parts:
  Parte2 = Arduino Mega 2560 (Rev3)
  PIR1 = PIR sensor

nets:
  N1: Parte2.D2_PWM, PIR1.SIG
  5V: Parte2.5V, PIR1.VDD
  GND: Parte2.GND, PIR1.GND
