# Fritzing sketch ULTRASONICO (saved by Fritzing 0.8.7b)
breadboards: 1

parts:
  U2 = HC-SR04 [chip_label=IC package="SIP (Single Inline) [THT]"]
  Parte1 = Arduino Mega 2560 (Rev3)

nets:
  VCC: U2.Vcc, Parte1.5V
  N1: U2.Trig, Parte1.D12_PWM
  N2: U2.Echo, Parte1.D11_PWM
  GND: U2.GND, Parte1.GND

custom parts:
  HC-SR04: HC-SR04 ultrasound distance sensor
